# Fritzing sketch AICS I2C 1MB EEPROM (saved by Fritzing 0.8.7b)
circuit board: 4.37116cm x 3.59668cm
breadboards: 1

parts:
  IC1 = 24LC1025 [package=THT]
  S1 = Toggle Switch [package=THT]
  S2 = Toggle Switch [package=THT]
  S3 = Toggle Switch [package=THT]
  S4_READONLY = Toggle Switch [package=THT]
  D1 = Rectifier Diode [part_number=1N4001 package="300 mil [THT]"]
  J1_V+/V- = Screw terminal - 2 pins [package=THT]
  J2_SDA_SCL = Screw terminal - 2 pins [package=THT]
  J3_SDA_SCL = Screw terminal - 2 pins [package=THT]

nets:
  N1: IC1.A0, S1.COM
  N2: IC1.A1, S2.COM
  N3: IC1.A2_(CS), S3.COM
  N4: IC1.0V, S1.L2, S2.L2, S3.L2, S4_READONLY.L2, J1_V+/V-.pin1
  N5: IC1.SDA_-_I2C_Data, J2_SDA_SCL.pin1, J3_SDA_SCL.pin2
  N6: IC1.SCL_-_I2C_Clock, J2_SDA_SCL.pin2, J3_SDA_SCL.pin1
  N7: IC1.WP_-_Write_Protect, S4_READONLY.COM
  N8: IC1.+V, S4_READONLY.L1, D1.cathode
  N9: S1.L1, S2.L1, S3.L1, D1.anode, J1_V+/V-.pin2

notes:
  OFF
  ON
  ArduICS
  1MB I2C
  EEPROM
  ADDRESS
