# Fritzing sketch AICS I2C 8IO (saved by Fritzing 0.8.7b)
circuit board: 6.13292cm x 4.51188cm
breadboards: 1

parts:
  U6 = PCF8574 [package="DIP16 [THT]"]
  J1_-/+/- = screw terminal, 3 pins
  J2_INT/SCL/SDA = screw terminal, 3 pins
  S1 = Toggle Switch [package=THT]
  S2 = Toggle Switch [package=THT]
  S3 = Toggle Switch [package=THT]
  LED1 = LED - 5mm [color="Red (633nm)" package="5 mm [THT]"]
  R1 = Resistor [tolerance=±5% resistance=220 package=THT]
  D0_D1_D2 = screw terminal, 3 pins
  D3_D4_D5 = screw terminal, 3 pins
  D6_D7_G = screw terminal, 3 pins

nets:
  N1: U6.A0, S1.COM
  N2: U6.A1, S2.COM
  N3: U6.A3, S3.COM
  N4: U6.P0, D0_D1_D2.pin3
  N5: U6.P1, D0_D1_D2.pin2
  N6: U6.P2, D0_D1_D2.pin1
  N7: U6.P3, D3_D4_D5.pin3
  N8: U6.GND, J1_-/+/-.pin1, J1_-/+/-.pin3, S1.L1, S2.L1, S3.L1, D6_D7_G.pin1
  N9: U6.P4, D3_D4_D5.pin2
  N10: U6.P5, D3_D4_D5.pin1
  N11: U6.P6, D6_D7_G.pin3
  N12: U6.P7, D6_D7_G.pin2
  N13: U6.INT, J2_INT/SCL/SDA.pin3
  N14: U6.SCL, J2_INT/SCL/SDA.pin2
  N15: U6.SDA, J2_INT/SCL/SDA.pin1
  N16: U6.VCC, J1_-/+/-.pin2, S1.L2, S2.L2, S3.L2, LED1.anode, R1.Pin_1
  N17: LED1.cathode, R1.Pin_0

notes:
  ArduICS I2C I/O
  Expander (8 Pin)
