# Fritzing sketch AICS I2C IOx16 (saved by Fritzing 0.8.7b)
circuit board: 8.82131cm x 4.6034cm
breadboards: 1

parts:
  IC1 = MCP23017 I2C I/O Expander
  S1 = Toggle Switch [package=THT]
  S2 = Toggle Switch [package=THT]
  S3 = Toggle Switch [package=THT]
  J1_+5V_/_+0V = Screw terminal - 2 pins [package=THT]
  J2_SCL/SDA = Screw terminal - 2 pins [package=THT]
  J3_GPB_7_6_5_4_3_2_1_0 = screw terminal, 8 pins
  J7_SCL/SDA = Screw terminal - 2 pins [package=THT]
  J3_GPA_7_6_5_4_3_2_1_0 = screw terminal, 8 pins
  J5_INT_A/B = Screw terminal - 2 pins [package=THT]
  RESET = Pushbutton [package="[THT]"]
  J5_SCL/SDA1 = Screw terminal - 2 pins [package=THT]

nets:
  N1: IC1.GPB0, J3_GPB_7_6_5_4_3_2_1_0.pin8
  N2: IC1.GPB1, J3_GPB_7_6_5_4_3_2_1_0.pin7
  N3: IC1.GPB2, J3_GPB_7_6_5_4_3_2_1_0.pin6
  N4: IC1.GPB3, J3_GPB_7_6_5_4_3_2_1_0.pin5
  N5: IC1.GPB4, J3_GPB_7_6_5_4_3_2_1_0.pin4
  N6: IC1.GPB5, J3_GPB_7_6_5_4_3_2_1_0.pin3
  N7: IC1.GPB6, J3_GPB_7_6_5_4_3_2_1_0.pin2
  N8: IC1.GPB7, J3_GPB_7_6_5_4_3_2_1_0.pin1
  N9: IC1.VDD, S1.L2, S2.L2, S3.L2, J1_+5V_/_+0V.pin2
  N10: IC1.VSS, S1.L1, S2.L1, S3.L1, J1_+5V_/_+0V.pin1, RESET.Pin_1, RESET.Pin_2, J5_SCL/SDA1.pin1, J5_SCL/SDA1.pin2
  N11: IC1.SCL, J2_SCL/SDA.pin2, J7_SCL/SDA.pin1
  N12: IC1.SDA, J2_SCL/SDA.pin1, J7_SCL/SDA.pin2
  N13: IC1.A0, S1.COM
  N14: IC1.A1, S2.COM
  N15: IC1.A2, S3.COM
  N16: IC1.RESET, RESET.Pin_3, RESET.Pin_4
  N17: IC1.INTB, J5_INT_A/B.pin2
  N18: IC1.INTA, J5_INT_A/B.pin1
  N19: IC1.GPA0, J3_GPA_7_6_5_4_3_2_1_0.pin8
  N20: IC1.GPA1, J3_GPA_7_6_5_4_3_2_1_0.pin7
  N21: IC1.GPA2, J3_GPA_7_6_5_4_3_2_1_0.pin6
  N22: IC1.GPA3, J3_GPA_7_6_5_4_3_2_1_0.pin5
  N23: IC1.GPA4, J3_GPA_7_6_5_4_3_2_1_0.pin4
  N24: IC1.GPA5, J3_GPA_7_6_5_4_3_2_1_0.pin3
  N25: IC1.GPA6, J3_GPA_7_6_5_4_3_2_1_0.pin2
  N26: IC1.GPA7, J3_GPA_7_6_5_4_3_2_1_0.pin1

notes:
  ADDR
  ArduICS I2C IO Board
  Set ADDR switches diffrently for each board
  Open Source Hardware
  25mA per pin
  J2/J7 passthru
  Created by
  SilverWingedSeraph

custom parts:
  MCP23017 I2C I/O Expander: MCP23017 I2C 16-Channel I/O Expander
