# Fritzing sketch AICS Motherboard Mk2 (saved by Fritzing 0.8.7b)
circuit board: 14.6809cm x 8.25871cm
breadboards: 1

parts:
  J1_Power = screw terminal, 3 pins [part_number=KF301-3P]
  U1 = Voltage Regulator - 5V [package="TO220 [THT]"]
  U2 = Voltage Regulator - 5V [package="TO220 [THT]"]
  U3 = Voltage Regulator - 5V [package="TO220 [THT]"]
  U4 = Voltage Regulator - 5V [package="TO220 [THT]"]
  C1 = Electrolytic Capacitor [capacitance=47µF voltage=50V part_number="Lelon 020-1670" package="200 mil [THT, electrolytic]"]
  C2 = Electrolytic Capacitor [capacitance=47µF voltage=50V part_number="Lelon 020-1670" package="200 mil [THT, electrolytic]"]
  D1 = Rectifier Diode [part_number=1N4001 package="300 mil [THT]"]
  D2 = Rectifier Diode [part_number=1N4001 package="300 mil [THT]"]
  D3 = Rectifier Diode [part_number=1N4001 package="300 mil [THT]"]
  Adafruit_Atmega32u4 = Adafruit Atmega32u4 Breakout Board [part_number="Atmega 32u4"]
  J2_SCK_MOSI_MISO = screw terminal, 3 pins [part_number=KF301-3P]
  J3_SRX_STX_RST = screw terminal, 3 pins [part_number=KF301-3P]
  R1 = Resistor [tolerance=±5% resistance=470k package=THT]
  R2 = Resistor [tolerance=±5% resistance=470k package=THT]
  R3 = Resistor [tolerance=±5% resistance=470k package=THT]
  J4_SDA_SCL_GND = screw terminal, 3 pins [part_number=KF301-3P]
  R4 = Resistor [tolerance=±5% resistance=470k package=THT]
  R5 = Resistor [tolerance=±5% resistance=470k package=THT]
  R6 = Resistor [tolerance=±5% resistance=470k package=THT]
  R7 = Resistor [tolerance=±5% resistance=470k package=THT]
  R8 = Resistor [tolerance=±5% resistance=470k package=THT]
  R9 = Resistor [tolerance=±5% resistance=470k package=THT]
  R10 = Resistor [tolerance=±5% resistance=470k package=THT]
  CTRL = LED - 5mm [color="Red (633nm)" package="5 mm [THT]"]
  R11 = Resistor [tolerance=±5% resistance=220 package=THT]
  K1 = Relay [part_number=FRS1B-S package=THT]
  K1_NO_C_NC = screw terminal, 3 pins [part_number=KF301-3P]
  K2 = Relay [part_number=FRS1B-S package=THT]
  K2_NO_C_NC = screw terminal, 3 pins [part_number=KF301-3P]
  K3 = Relay [part_number=FRS1B-S package=THT]
  K3_NO_C_NC = screw terminal, 3 pins [part_number=KF301-3P]
  R12 = Resistor [tolerance=±5% resistance=220 package=THT]
  R13 = Resistor [tolerance=±5% resistance=220 package=THT]
  R14 = Resistor [tolerance=±5% resistance=220 package=THT]
  J5_A3_A2_A1 = screw terminal, 3 pins [part_number=KF301-3P]
  J6_A0_D13_D5 = screw terminal, 3 pins [part_number=KF301-3P]
  R15 = Resistor [tolerance=±5% resistance=220 package=THT]
  PWR = LED - 5mm [color="Red (633nm)" package="5 mm [THT]"]
  J7_D8_D3_D2 = screw terminal, 3 pins
  J8_GND = screw terminal, 3 pins [part_number=KF301-3P]
  J9_+5V = screw terminal, 3 pins [part_number=KF301-3P]
  C3 = Tantalum Capacitor [capacitance=4.7µF voltage=50V package="100 mil [THT, tantalum]"]
  TRS1 = Audio Jack (TRS) 3.5mm [part_number=CP1-3555NG-ND package="4Ucon 08780 [THT]"]

nets:
  N1: J1_Power.pin1, U1.output_voltage, U2.output_voltage, U3.output_voltage, U4.output_voltage, C1.+, C2.+, D2.anode, J9_+5V.pin1, J9_+5V.pin2, J9_+5V.pin3
  N2: J1_Power.pin2, U1.input_voltage, U2.input_voltage, U3.input_voltage, U4.input_voltage, C3.+
  N3: J1_Power.pin3, D1.cathode, C3.-
  GND: U1.GND, U2.GND, U3.GND, U4.GND, C1.-, C2.-, D1.anode, D3.cathode
  N4: D2.cathode, Adafruit_Atmega32u4.5V, R15.Pin_0, PWR.anode
  N5: D3.anode, R1.Pin_1, R2.Pin_1, R3.Pin_1, J4_SDA_SCL_GND.pin1, R4.Pin_1, R5.Pin_1, R6.Pin_1, R7.Pin_1, R8.Pin_1, R9.Pin_1, R10.Pin_1, R11.Pin_1, K1.COIL1, K2.COIL1, K3.COIL1, J8_GND.pin1, J8_GND.pin2, J8_GND.pin3, TRS1.Sleeve
  N6: Adafruit_Atmega32u4.F0, J4_SDA_SCL_GND.pin3, R8.Pin_0
  N7: Adafruit_Atmega32u4.F1, J4_SDA_SCL_GND.pin2, R7.Pin_0
  N8: Adafruit_Atmega32u4.F4, J5_A3_A2_A1.pin1
  N9: Adafruit_Atmega32u4.F5, J5_A3_A2_A1.pin2
  N10: Adafruit_Atmega32u4.F6, J5_A3_A2_A1.pin3
  N11: Adafruit_Atmega32u4.F7, J6_A0_D13_D5.pin1
  N12: Adafruit_Atmega32u4.C7, J6_A0_D13_D5.pin2
  N13: Adafruit_Atmega32u4.C6, J6_A0_D13_D5.pin3
  N14: Adafruit_Atmega32u4.B7, R14.Pin_1
  N15: Adafruit_Atmega32u4.B6, R13.Pin_1
  N16: Adafruit_Atmega32u4.B5, R12.Pin_1
  N17: Adafruit_Atmega32u4.B4, J7_D8_D3_D2.pin1
  N18: Adafruit_Atmega32u4.E6, CTRL.anode
  N19: Adafruit_Atmega32u4.B1, J2_SCK_MOSI_MISO.pin3, R2.Pin_0
  N20: Adafruit_Atmega32u4.B2, J2_SCK_MOSI_MISO.pin2, R1.Pin_0
  N21: Adafruit_Atmega32u4.B3, J2_SCK_MOSI_MISO.pin1, R3.Pin_0
  N22: Adafruit_Atmega32u4.D0, J7_D8_D3_D2.pin2
  N23: Adafruit_Atmega32u4.D1, J7_D8_D3_D2.pin3
  N24: Adafruit_Atmega32u4.D2, J3_SRX_STX_RST.pin3
  N25: Adafruit_Atmega32u4.D3, J3_SRX_STX_RST.pin2, R5.Pin_0
  N26: Adafruit_Atmega32u4.D6, R10.Pin_0, TRS1.Tip
  N27: Adafruit_Atmega32u4.D7, R9.Pin_0, TRS1.Ring
  N28: Adafruit_Atmega32u4.RST, J3_SRX_STX_RST.pin1, R4.Pin_0, R6.Pin_0
  N29: CTRL.cathode, R11.Pin_0
  N30: K1.A, K1_NO_C_NC.pin1
  N31: K1.C1, K1.C2, K1_NO_C_NC.pin2
  N32: K1.COIL2, R12.Pin_0
  N33: K1.B, K1_NO_C_NC.pin3
  N34: K2.A, K2_NO_C_NC.pin1
  N35: K2.C1, K2.C2, K2_NO_C_NC.pin2
  N36: K2.COIL2, R13.Pin_0
  N37: K2.B, K2_NO_C_NC.pin3
  N38: K3.A, K3_NO_C_NC.pin1
  N39: K3.C1, K3.C2, K3_NO_C_NC.pin2
  N40: K3.COIL2, R14.Pin_0
  N41: K3.B, K3_NO_C_NC.pin3
  N42: R15.Pin_1, PWR.cathode

notes:
  - / + / TAP
  Power Supply
  4 Amps Maximum
  20 Volts Maximum
  XPAND: 12 CLK / 6 DATA
  TIP CLK RING DATA
  ArduICS Mk2
  K1:D9|K2:D10|K3:D11
  2.2mm 10x3.2 cm apart
