# Fritzing sketch AICS Peripheral Power Supply (saved by Fritzing 0.8.7b)
circuit board: 7.50571cm x 5.061cm
breadboards: 1

parts:
  U1 = Voltage Regulator - 5V [package="TO220 [THT]"]
  U2 = Voltage Regulator - 5V [package="TO220 [THT]"]
  U3 = Voltage Regulator - 5V [package="TO220 [THT]"]
  U4 = Voltage Regulator - 5V [package="TO220 [THT]"]
  U5 = Voltage Regulator - 5V [package="TO220 [THT]"]
  U6 = Voltage Regulator - 5V [package="TO220 [THT]"]
  U7 = Voltage Regulator - 5V [package="TO220 [THT]"]
  U8 = Voltage Regulator - 5V [package="TO220 [THT]"]
  C1 = Electrolytic Capacitor [capacitance=4.7mF voltage=20V package="200 mil [THT, electrolytic]"]
  C2 = Electrolytic Capacitor [capacitance=4.7mF voltage=20V package="200 mil [THT, electrolytic]"]
  J2_OUT_+/- = screw terminal, 8 pins
  J1_IN_+_/_- = Screw terminal - 2 pins [package=THT]
  R1 = Resistor [tolerance=±5% resistance=220 package=THT]
  LED1 = LED - 5mm [color="Red (633nm)" package="5 mm [THT]"]

nets:
  N1: U1.input_voltage, U2.input_voltage, U3.input_voltage, U4.input_voltage, U5.input_voltage, U6.input_voltage, U7.input_voltage, U8.input_voltage, C2.+, J1_IN_+_/_-.pin2
  GND: U1.GND, U2.GND, U3.GND, U4.GND, U5.GND, U6.GND, U7.GND, U8.GND, C1.-, C2.-, J2_OUT_+/-.pin2, J2_OUT_+/-.pin4, J2_OUT_+/-.pin6, J2_OUT_+/-.pin8, J1_IN_+_/_-.pin1, R1.Pin_0
  N2: U1.output_voltage, U2.output_voltage, U3.output_voltage, U4.output_voltage, C1.+, J2_OUT_+/-.pin1, J2_OUT_+/-.pin3, J2_OUT_+/-.pin5, J2_OUT_+/-.pin7, LED1.anode
  N3: U5.output_voltage, U6.output_voltage, U7.output_voltage, U8.output_voltage
  N4: R1.Pin_1, LED1.cathode

notes:
  ArduICS Power
  Output 5V 8A
  Input 6V - 12V 8.5A
  Made With Fritzing
  by SilverWingedSeraph
