# Fritzing sketch AICS SPI RTC (saved by Fritzing 0.8.7b)
circuit board: 4.6114cm x 3.01324cm
breadboards: 1

parts:
  IC1 = DS1302 [package="DIP8 [THT]"]
  BAT1_12mm_3/3_7_V = Battery Holders [package=battcon_12mm_pth]
  XTAL1 = Crystal [frequency="32 MHz" package=THT]
  J1_+/-/CS = screw terminal, 3 pins
  J2_SCLK_SDAT_N = screw terminal, 3 pins

nets:
  N1: IC1.+V, J1_+/-/CS.pin3
  N2: IC1.X1_-_Crystal, XTAL1.pin_1
  N3: IC1.X2_-_Crystal, XTAL1.pin_0
  N4: IC1.0V, BAT1_12mm_3/3_7_V.-, J1_+/-/CS.pin2
  N5: IC1.CE_-_Chip_Enable, J1_+/-/CS.pin1
  N6: IC1.I/O_-_SPI_Data_In/Out, J2_SCLK_SDAT_N.pin2
  N7: IC1.SCLK_-_SPI_Clock, J2_SCLK_SDAT_N.pin3
  N8: IC1.Vbat_-_Backup_Supply, BAT1_12mm_3/3_7_V.+

notes:
  SPI RTC 0.1a
  ArduICS by
  SilverWingedSeraph
