# Fritzing sketch XPAND General (saved by Fritzing 0.8.7b)
circuit board: 7.1646cm x 5.80887cm
breadboards: 1

parts:
  XPAND_IN = Audio Jack (TRS) 3.5mm [package="4Ucon 08780 [THT]"]
  XPAND_OUT = Audio Jack (TRS) 3.5mm [package="4Ucon 08780 [THT]"]
  U1 = 74HC595 [package="DIP16 [THT]"]
  -_/_+ = Screw terminal - 2 pins [package=THT]
  D1 = Rectifier Diode [part_number=1N4001 package="300 mil [THT]"]
  J1_0/1/2/3/4/5/6/7/G = screw terminal, 9 pins
  D2 = Rectifier Diode [part_number=1N4001 package="300 mil [THT]"]
  D3 = Rectifier Diode [part_number=1N4001 package="300 mil [THT]"]
  D4 = Rectifier Diode [part_number=1N4001 package="300 mil [THT]"]
  D5 = Rectifier Diode [part_number=1N4001 package="300 mil [THT]"]
  D6 = Rectifier Diode [part_number=1N4001 package="300 mil [THT]"]
  D7 = Rectifier Diode [part_number=1N4001 package="300 mil [THT]"]
  D8 = Rectifier Diode [part_number=1N4001 package="300 mil [THT]"]
  D9 = Rectifier Diode [part_number=1N4001 package="300 mil [THT]"]
  PWR = LED - 5mm [color="Red (633nm)" package="5 mm [THT]"]

nets:
  N1: XPAND_IN.Sleeve, XPAND_OUT.Sleeve
  N2: XPAND_IN.Ring, U1.DS
  N3: XPAND_IN.Tip, XPAND_OUT.Tip, U1.SH_CP
  N4: XPAND_OUT.Ring, U1.Q7'
  N5: U1.Q1, D3.anode
  N6: U1.Q2, D4.anode
  N7: U1.Q3, D5.anode
  N8: U1.Q4, D6.anode
  N9: U1.Q5, D7.anode
  N10: U1.Q6, D8.anode
  N11: U1.Q7, D9.anode
  N12: U1.GND, U1.OE, -_/_+.pin1, J1_0/1/2/3/4/5/6/7/G.pin1, PWR.cathode
  N13: U1.Q0, D2.anode
  N14: U1.VCC, D1.cathode
  N15: -_/_+.pin2, D1.anode, PWR.anode
  N16: J1_0/1/2/3/4/5/6/7/G.pin2, D9.cathode
  N17: J1_0/1/2/3/4/5/6/7/G.pin3, D8.cathode
  N18: J1_0/1/2/3/4/5/6/7/G.pin4, D7.cathode
  N19: J1_0/1/2/3/4/5/6/7/G.pin5, D6.cathode
  N20: J1_0/1/2/3/4/5/6/7/G.pin6, D5.cathode
  N21: J1_0/1/2/3/4/5/6/7/G.pin7, D4.cathode
  N22: J1_0/1/2/3/4/5/6/7/G.pin8, D3.cathode
  N23: J1_0/1/2/3/4/5/6/7/G.pin9, D2.cathode

notes:
  TIP CLK RING DATA
  ArduICS
  XPAND General
  Output Board
  Version 0.1a
  This Board Is Liberated
  Created by SilverWingedSeraph
  Open Source Hardware
  standoffs!
  Mount on
