# Fritzing sketch XPAND LED (saved by Fritzing 0.8.7b)
circuit board: 7.1646cm x 5.80887cm
breadboards: 1

parts:
  XPAND_IN = Audio Jack (TRS) 3.5mm [package="4Ucon 08780 [THT]"]
  XPAND_OUT = Audio Jack (TRS) 3.5mm [package="4Ucon 08780 [THT]"]
  U1 = 74HC595 [package="DIP16 [THT]"]
  -_/_+ = Screw terminal - 2 pins [package=THT]
  D1 = Rectifier Diode [part_number=1N4001 package="300 mil [THT]"]
  PWR = LED - 5mm [color="Red (633nm)" package="5 mm [THT]"]
  LED1 = LED - 5mm [color="Red (633nm)" package="5 mm [THT]"]
  LED2 = LED - 5mm [color="Red (633nm)" package="5 mm [THT]"]
  LED3 = LED - 5mm [color="Red (633nm)" package="5 mm [THT]"]
  LED4 = LED - 5mm [color="Red (633nm)" package="5 mm [THT]"]
  LED5 = LED - 5mm [color="Red (633nm)" package="5 mm [THT]"]
  LED6 = LED - 5mm [color="Red (633nm)" package="5 mm [THT]"]
  LED7 = LED - 5mm [color="Red (633nm)" package="5 mm [THT]"]
  LED8 = LED - 5mm [color="Red (633nm)" package="5 mm [THT]"]
  R1 = Resistor [tolerance=±5% resistance=220 package=THT]
  R2 = Resistor [tolerance=±5% resistance=220 package=THT]
  R3 = Resistor [tolerance=±5% resistance=220 package=THT]
  R4 = Resistor [tolerance=±5% resistance=220 package=THT]
  R5 = Resistor [tolerance=±5% resistance=220 package=THT]
  R6 = Resistor [tolerance=±5% resistance=220 package=THT]
  R7 = Resistor [tolerance=±5% resistance=220 package=THT]
  R8 = Resistor [tolerance=±5% resistance=220 package=THT]

nets:
  N1: XPAND_IN.Sleeve, XPAND_OUT.Sleeve
  N2: XPAND_IN.Ring, U1.DS
  N3: XPAND_IN.Tip, XPAND_OUT.Tip, U1.SH_CP
  N4: XPAND_OUT.Ring, U1.Q7'
  N5: U1.Q1, R2.Pin_0
  N6: U1.Q2, R3.Pin_0
  N7: U1.Q3, R4.Pin_0
  N8: U1.Q4, R5.Pin_0
  N9: U1.Q5, R6.Pin_0
  N10: U1.Q6, R7.Pin_0
  N11: U1.Q7, R8.Pin_0
  N12: U1.GND, -_/_+.pin1, PWR.cathode, LED1.cathode, LED2.cathode, LED3.cathode, LED4.cathode, LED5.cathode, LED6.cathode, LED7.cathode, LED8.cathode
  N13: U1.Q0, R1.Pin_0
  N14: U1.VCC, D1.cathode
  N15: -_/_+.pin2, D1.anode, PWR.anode
  N16: LED1.anode, R1.Pin_1
  N17: LED2.anode, R2.Pin_1
  N18: LED3.anode, R3.Pin_1
  N19: LED4.anode, R4.Pin_1
  N20: LED5.anode, R5.Pin_1
  N21: LED6.anode, R6.Pin_1
  N22: LED7.anode, R7.Pin_1
  N23: LED8.anode, R8.Pin_1

notes:
  TIP CLK RING DATA
  ArduICS
  XPAND LED
  Output Board
  Version 0.1a
  Open Source Hardware
  This Board Is Liberated
  Created by SilverWingedSeraph
  standoffs!
  Mount on
