# Fritzing sketch XPAND Relay (saved by Fritzing 0.8.7b)
circuit board: 7.39539cm x 10.8589cm
breadboards: 1

parts:
  XPAND_IN = Audio Jack (TRS) 3.5mm [package="4Ucon 08780 [THT]"]
  XPAND_OUT = Audio Jack (TRS) 3.5mm [package="4Ucon 08780 [THT]"]
  U1 = 74HC595 [package="DIP16 [THT]"]
  -_/_+ = Screw terminal - 2 pins [package=THT]
  D1 = Rectifier Diode [part_number=1N4001 package="300 mil [THT]"]
  PWR = LED - 5mm [color="Red (633nm)" package="5 mm [THT]"]
  R1 = Resistor [tolerance=±5% resistance=220 package=THT]
  R2 = Resistor [tolerance=±5% resistance=220 package=THT]
  R3 = Resistor [tolerance=±5% resistance=220 package=THT]
  R4 = Resistor [tolerance=±5% resistance=220 package=THT]
  R5 = Resistor [tolerance=±5% resistance=220 package=THT]
  R6 = Resistor [tolerance=±5% resistance=220 package=THT]
  R7 = Resistor [tolerance=±5% resistance=220 package=THT]
  R8 = Resistor [tolerance=±5% resistance=220 package=THT]
  K1 = Relay [part_number=FRS1B-S package=THT]
  K2 = Relay [part_number=FRS1B-S package=THT]
  K3 = Relay [part_number=FRS1B-S package=THT]
  K4 = Relay [part_number=FRS1B-S package=THT]
  K8 = Relay [part_number=FRS1B-S package=THT]
  K7 = Relay [part_number=FRS1B-S package=THT]
  K6 = Relay [part_number=FRS1B-S package=THT]
  K5 = Relay [part_number=FRS1B-S package=THT]
  J1 = screw terminal, 3 pins
  J2 = screw terminal, 3 pins
  J3 = screw terminal, 3 pins
  J4 = screw terminal, 3 pins
  J5 = screw terminal, 3 pins
  J6 = screw terminal, 3 pins
  J7 = screw terminal, 3 pins
  J8 = screw terminal, 3 pins

nets:
  N1: XPAND_IN.Sleeve, XPAND_OUT.Sleeve
  N2: XPAND_IN.Ring, U1.DS
  N3: XPAND_IN.Tip, XPAND_OUT.Tip, U1.SH_CP
  N4: XPAND_OUT.Ring, U1.Q7'
  N5: U1.Q1, R2.Pin_0
  N6: U1.Q2, R3.Pin_0
  N7: U1.Q3, R4.Pin_0
  N8: U1.Q4, R5.Pin_0
  N9: U1.Q5, R6.Pin_0
  N10: U1.Q6, R7.Pin_0
  N11: U1.Q7, R8.Pin_0
  N12: U1.GND, U1.OE, -_/_+.pin1, PWR.cathode, K1.COIL1, K2.COIL1, K3.COIL1, K4.COIL1, K8.COIL2, K7.COIL2, K6.COIL2, K5.COIL2
  N13: U1.Q0, R1.Pin_0
  N14: U1.VCC, D1.cathode
  N15: -_/_+.pin2, D1.anode, PWR.anode
  N16: R1.Pin_1, K1.COIL2
  N17: R2.Pin_1, K2.COIL2
  N18: R3.Pin_1, K3.COIL2
  N19: R4.Pin_1, K4.COIL2
  N20: R5.Pin_1, K5.COIL1
  N21: R6.Pin_1, K6.COIL1
  N22: R7.Pin_1, K7.COIL1
  N23: R8.Pin_1, K8.COIL1
  N24: K1.A, J1.pin1
  N25: K1.C1, K1.C2, J1.pin2
  N26: K1.B, J1.pin3
  N27: K2.A, J2.pin1
  N28: K2.C1, K2.C2, J2.pin2
  N29: K2.B, J2.pin3
  N30: K3.A, J3.pin1
  N31: K3.C1, K3.C2, J3.pin2
  N32: K3.B, J3.pin3
  N33: K4.A, J4.pin1
  N34: K4.C1, K4.C2, J4.pin2
  N35: K4.B, J4.pin3
  N36: K8.A, J8.pin1
  N37: K8.C1, K8.C2, J8.pin2
  N38: K8.B, J8.pin3
  N39: K7.A, J7.pin1
  N40: K7.C1, K7.C2, J7.pin2
  N41: K7.B, J7.pin3
  N42: K6.A, J6.pin1
  N43: K6.C1, J6.pin2
  N44: K6.B, J6.pin3
  N45: K5.A, J5.pin1
  N46: K5.C1, K5.C2, J5.pin2
  N47: K5.B, J5.pin3

notes:
  TIP CLK RING DATA
  ArduICS
  XPAND Relay
  Output Board
  Version 0.1a
  Open Source Hardware
  This Board Is Liberated
  Created by SilverWingedSeraph
  standoffs!
  Mount on
  NC C NO
  CAUTION
  HIGH
  VOLTAGE
  SWITCHING
